# Fritzing sketch Synth-DIY_Workstation_Schaltplan (saved by Fritzing 0.9.3b)
breadboards: 3

parts:
  Bauteil1 = Arduino Nano (Rev3.0)  # not connected
  U1 = MIDI_CONN_FEMALE_SUPPORT [package=din_5_female_support]  # not connected
  U4 = 74HC595 [package="DIP16 [THT]"]  # not connected
  U5 = 74HC595 [package="DIP16 [THT]"]  # not connected
  U9 = 74HC595 [package="DIP16 [THT]"]  # not connected
  U10 = MIDI_CONN_FEMALE_SUPPORT [package=din_5_female_support]  # not connected
  R1 = Rotary Potentiometer (Small) [maximum_resistance=100kΩ package=THT]  # not connected
  VCC1 = Battery  # not connected
  Power_plug1 = Power plug  # not connected
  TRS1 = Audio Jack (TRS) 3.5mm [package="4Ucon 08780 [THT]"]  # not connected
  SW1 = ENCODER_RGB_CA [package=encoder_led_3]  # not connected
  SP1 = SPEAKER [package=pcb_mount_speaker]  # not connected
  S1 = Round Pushbutton  # not connected
  R3 = Rotary Potentiometer (Small) [maximum_resistance=100kΩ package=THT]  # not connected
  S2 = Round Pushbutton  # not connected
  R4 = Rotary Potentiometer (Small) [maximum_resistance=100kΩ package=THT]  # not connected
  S3 = Round Pushbutton  # not connected
  R5 = Rotary Potentiometer (Small) [maximum_resistance=100kΩ package=THT]  # not connected
  S4 = Round Pushbutton  # not connected
  R6 = Rotary Potentiometer (Small) [maximum_resistance=100kΩ package=THT]  # not connected
  S5 = Round Pushbutton  # not connected
  R7 = Rotary Potentiometer (Small) [maximum_resistance=100kΩ package=THT]  # not connected
  S6 = Round Pushbutton  # not connected
  R8 = Rotary Potentiometer (Small) [maximum_resistance=100kΩ package=THT]  # not connected
  S7 = Round Pushbutton  # not connected
  R9 = Rotary Potentiometer (Small) [maximum_resistance=100kΩ package=THT]  # not connected
  S8 = Round Pushbutton  # not connected
  S9 = Round Pushbutton  # not connected
  S10 = Round Pushbutton  # not connected
  S11 = Round Pushbutton  # not connected
  S12 = Round Pushbutton  # not connected
  S13 = Round Pushbutton  # not connected
  J1 = shrouded pin header, 10 pins [form="♂ (shrouded male)"]  # not connected
  S14 = Round Pushbutton  # not connected
  S15 = Round Pushbutton  # not connected
  VCC2 = Battery  # not connected
  Bauteil2 = Analog Digital MUX Breakout  # not connected
  Bauteil3 = Analog Digital MUX Breakout  # not connected
  Bauteil4 = Adafruit Analog 2-Axis Joystick [part_number="Adafruit #512"]  # not connected
  Bauteil5 = 14-segment LED Alphanumeric Backpack [part_number=2157]  # not connected
  Bauteil6 = Trellis Monochrome Driver PCB for 4x4 Keypad and 3mm LEDs [part_number=1616]  # not connected
  Bauteil7 = Adafruit PiTFT Plus 2.8inch [part_number="Adafruit #2298 and #2423"]  # not connected
  TRS2 = Audio Jack (TRS) 3.5mm [package="4Ucon 08780 [THT]"]  # not connected
  Bauteil8 = Adafruit Pi Cobbler [part_number="Adafruit #914"]
  IC1 = MCP3008 8-channel 10-bit ADC [part_number=MCP3008]
  Raspberry_Pi1 = Raspberry Pi B rev2  # not connected
  Bauteil9 = 14-segment LED Alphanumeric Backpack [part_number=2157]  # not connected
  Bauteil10 = Trellis Monochrome Driver PCB for 4x4 Keypad and 3mm LEDs [part_number=1616]  # not connected
  Bauteil11 = 16-Channel 12-bit PWM Servo Driver - I2C [part_number=815]  # not connected
  Bauteil12 = Arduino Uno (Rev3) - ICSP  # not connected
  Bauteil13 = Memoire 1.0 - SD card log shield  # not connected
  Bauteil14 = Adafruit MCP4725 Breakout Board - 12-Bit DAC [part_number="Adafruit #935"]  # not connected
  NEOPIXEL1 = Neopixel Strip -- White (60/m)
  LED1 = RGB LED - (4 legs) [package="5 mm [THT]"]  # not connected
  IC2 = Voltage Regulator [package=to-220-alt]  # not connected
  U11 = V_REG_LD1117VXX [package=78xxl]  # not connected
  D1 = Rectifier Diode [part_number=1N4001 package="Melf DO-213 AB [SMD]"]  # not connected
  Bauteil15 = Logic Level Converter  # not connected
  LPD8806_RGB_LED_Strip1 = LPD8806 RGB LED Strip
  C2 = Electrolytic Capacitor [capacitance=1mF package="100 mil [THT, electrolytic]"]
  R11 = Resistor [tolerance=±5% resistance=470 package=THT]
  JACK1 = 2.1mm Barrel Jack with Terminal Block

nets:
  N1: Bauteil8.5.0V, LPD8806_RGB_LED_Strip1.+5V
  GND: Bauteil8.GND, IC1.no_name_yet#9, IC1.no_name_yet#14, LPD8806_RGB_LED_Strip1.GND
  N2: Bauteil8.CE0, IC1.no_name_yet#10
  N3: Bauteil8.3.3V, IC1.no_name_yet#15, IC1.no_name_yet#16
  N4: Bauteil8.MOSI, IC1.no_name_yet#11, LPD8806_RGB_LED_Strip1.DI
  N5: Bauteil8.MISO, IC1.no_name_yet#12
  N6: Bauteil8.SCLK, IC1.no_name_yet#13, LPD8806_RGB_LED_Strip1.CI
  N7: NEOPIXEL1.GND, C2.-, JACK1.NEG
  N8: NEOPIXEL1.DO, R11.Pin_0
  N9: NEOPIXEL1.+5V, C2.+, JACK1.POS

notes:
  MFOS 3-Ch. Amplifier
  MFOS Alien Screamer
  Noise Toaster
  Soundblaster Play
  WLAN
  BT
  USB-Hub
  Netzteil(e):
  USB-Hub --> Arduino, Raspberry (700 mAh !)
  9V MFOS
  5V Neopixels (32*3*30 mAh = 3 Ah)
  - - - - - - - - -
  Battery Pack:
  4 x Eneloop (4.8V)
  4 x Duracell (6V)
  USB-Power-Bank (5V @ 1A, 2A, bis 10.000Ah)
  UBEC (5V @ 3A)
  Voltage Regulators:
  LM1117 (3.3V out)
  L7805 (5V out)
  voltage divider:
  Vin - R1 - R2 -Vout
  5V - R2k - R1k - 3.3V
  5V -R470 - R330 - 3.3V
  https://learn.sparkfun.com/tutorials/voltage-dividers
  Level Shifters:
  74AHCT125 (quad 3 to 5V)
  PWM
  CV/ Gate
  LED dimming
  RGB-LED
  Servos
  Audio/ Tone Generation
  Products
  Adafruit 16-Channel 12-bit PWM/Servo Shield - I2C 0x40
  https://www.adafruit.com/product/1411
  https://www.adafruit.com/product/815
  Tutorial Arduino
  https://learn.adafruit.com/16-channel-pwm-servo-driver
  Tutorial Raspberry Pi
  https://learn.adafruit.com/adafruit-16-channel-servo-driver-with-raspberry-pi/overview
  Rii Keyboard
  Python
  Pygame
  https://learn.adafruit.com/raspberry-pi-pygame-ui-basics
  cwiid
  Pure Data, libpd
  TouchOSC
  Wiimote
  Mini Beamer
  LED-Strips
  Neopixels Uberguide
  https://learn.adafruit.com/adafruit-neopixel-uberguide/best-practices
  Data-PIN with Resistor 470 Ohm,
  Capacitor 1000uF (6,3V) accross +/- of power source
  Tutorial Arduino
  https://learn.adafruit.com/neopixel-painter/overview
  Tutorial Raspberry Pi
  https://learn.adafruit.com/neopixels-on-raspberry-pi/wiring
  Data-PIN of Neopixels to GPIO18 (PWM) on RPi with rpi_ws281x library
  Level-Converter Chip 74AHCT125
  - - - - - -
  DotStar
  https://learn.adafruit.com/adafruit-dotstar-leds
  Tutorial
  https://learn.adafruit.com/dotstar-pi-painter/overview
  - - - - - -
  LPD8806
  https://learn.adafruit.com/digital-led-strip
  The board’s MOSI pin connects to the DI pin on the LED strip,
  and SCLK connects to the CI pin.
  Tutorial
  https://learn.adafruit.com/light-painting-with-raspberry-pi/overview
  Boblight
  ?
  ADC
  MCP3008 (via SPI)
  https://www.adafruit.com/product/856
  erik-bartmann.de/wp-content/plugins/download-attachments/includes/download.php?id=184
  Adafruit Tutorial
  https://learn.adafruit.com/raspberry-pi-analog-to-digital-converters/overview
  Library
  https://github.com/adafruit/Adafruit_Python_MCP3008
  Resistors:
  10k pullups
  LED-Vrowiderstand 220 - 1000 Ohm
  Capacitors:
  10uF über Power Supply
  1000uF bei Neopixels
  MUX (Multiplexer) CD74HC4067
  https://www.sparkfun.com/products/9056
  Tutorial
  http://bildr.org/2011/02/cd74hc4067-arduino/
  Shift Register 74HC595
  https://www.sparkfun.com/products/13699
  Tutorial
  https://learn.sparkfun.com/tutorials/shift-registers
  Adafruit Quad-Alphanumeric Display 0,54" 14-segments (I2C 0x70)
  https://www.adafruit.com/product/2157
  Tutorial
  https://learn.adafruit.com/adafruit-led-backpack/0-54-alphanumeric
  Adafruit Trellis (I2C 0x70 change to 0x72)
  https://www.adafruit.com/product/1616
  https://www.adafruit.com/product/1611
  Tutorial
  https://learn.adafruit.com/adafruit-trellis-diy-open-source-led-keypad/overview
  I2C
  A4 - SDA
  A5 - SCL
  5V
  3.3V

custom parts:
  Adafruit Analog 2-Axis Joystick: This mini-kit makes it easy to mount a PSP/Xbox-like thumb joystick to your project. The thumbstick is an analog joystick - more accurate and sensitive than just 'directional' joysticks - with a 'press in to select' button. Since it's analog, you'll need two analog reading pins on your microcontroller to determine X and Y. Having an extra digital input will let you read the switch. The pack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
  14-segment LED Alphanumeric Backpack: This is a nice, bright alphanumeric display that shows letters and numbers. It's super bright and designed for viewing from distances up to 23 feet (7 meters) away. Four digits with 14 segments on a black surface and we give you a set of two alphanumeric displays as well as a driver board so you can make a clock or a four letter word. Like our other LED backpacks, these are end-to-end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
  Trellis Monochrome Driver PCB for 4x4 Keypad and 3mm LEDs: Trellis is an open source backlight keypad driver system. It is easy to use, works with any 3mm LEDs and eight tiles can be tiled together on a shared I2C bus. This PCB is specially made to match the Adafruit 4x4 elastomer keypad. Each Trellis PCB has 4x4 pads and 4x4 matching spots for 3mm LEDs. The circuitry on-board handles the background key-presses and LED lighting for the 4x4 tile.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
  Adafruit PiTFT Plus 2.8inch: Is this not the cutest little display for the Raspberry Pi? It features a 2.8" display with 320x240 16-bit color pixels and a resistive touch overlay. The plate uses the high speed SPI interface on the Pi and can use the mini display as a console, X window port, displaying images or video etc. Best of all it plugs right in on top! This updated design fits perfectly onto the Pi Zero, Pi 3, Pi 2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
  Adafruit Pi Cobbler: Now that you've finally got your hands on a Raspberry Pi® Model B , you're probably itching to make some fun embedded computer projects with it. What you need is an add on prototyping Pi Cobbler from Adafruit, which can break out all those tasty power, GPIO, I2C and SPI pins from the 26 pin header onto a solderless breadboard. This set will make "cobbling together" prototypes with the Pi super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
  16-Channel 12-bit PWM Servo Driver - I2C: You want to make a cool robot, maybe a hexapod walker, or maybe just a piece of art with a lot of moving parts. Or maybe you want to drive a lot of LEDs with precise PWM output. Using only two pins, control 16 free-running PWM outputs! You can even chain up 62 breakouts to control up to 992 PWM outputs.
  Adafruit MCP4725 Breakout Board - 12-Bit DAC: Your microcontroller probably has an ADC (analog -> digital converter) but does it have a DAC (digital -> analog converter)??? Now it can! This breakout board features the easy-to-use MCP4725 12-bit DAC. Control it via I2C and send it the value you want it to output, and the VOUT pin will have it. Great for audio / analog projects, such as when you can't use PWM but need a sine wave or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
  Neopixel Strip -- White (60/m): Neopixel Strip, White, 60 pixels per meter.
  LPD8806 RGB LED Strip: Digitally addressable RGB LED strip
