# Fritzing sketch ESP8266 (saved by Fritzing 0.9.2b)
breadboards: 1

parts:
  D1 = Rectifier Diode [part_number=1N4001 package="300 mil [THT]"]  # not connected
  R1 = Rotary Potentiometer (Small) [maximum_resistance=100kΩ package=THT]  # not connected
  S1 = Pushbutton [package="[THT]"]
  LED1 = RGB LED (com. cathode, rgb) [package="5 mm [THT]"]  # not connected
  LED2 = LED - 5mm [color="Red (633nm)" package="5 mm [THT]"]  # not connected
  J1 = Piezo Speaker  # not connected
  VCC1 = Battery  # not connected
  U1 = Voltage Regulator - 5V [package="TO220 [THT]"]  # not connected
  Bauteil1 = Arduino Nano (Rev3.0)  # not connected
  Bauteil2 = Logic Level Converter  # not connected
  U2 = Alphanumeric LED Display [package=alphanumeric]  # not connected
  BATT1 = 4xAA Switchable Battery Pack w/JST connector  # not connected
  7SEG1 = 7-Segment LED I2C Backpack (yellow)  # not connected
  Bauteil3 = HUZZAH ESP8266 Breakout  # not connected
  USBTTL1 = USB TTL Serial Cable  # not connected
  NEOPIXEL1 = Neopixel Strip -- White (60/m)  # not connected
  U3 = V_REG_LD1117VXX [package=78xxl]  # not connected
  C1 = Ceramic Capacitor [capacitance=100nF package="100 mil [THT, multilayer]"]  # not connected
  C2 = Electrolytic Capacitor [capacitance=1µF package="100 mil [THT, electrolytic]"]  # not connected
  JACK1 = 2.1mm Barrel Jack with Terminal Block  # not connected
  PSU1 = Adjustable Breadboard Power Supply  # not connected
  VCC2 = Battery block 9V  # not connected
  R2 = Resistor [tolerance=±5% resistance=470 package=THT]  # not connected
  C3 = Electrolytic Capacitor [capacitance=1mF package="100 mil [THT, electrolytic]"]  # not connected
  R3 = Resistor [tolerance=±5% resistance=220 package=THT]  # not connected
  R4 = Resistor [tolerance=±5% resistance=220 package=THT]  # not connected
  R5 = Resistor [tolerance=±5% resistance=220 package=THT]  # not connected
  R6 = Resistor [tolerance=±5% resistance=220 package=THT]  # not connected

nets:
  N1: S1.Pin_1, S1.Pin_2
  N2: S1.Pin_3, S1.Pin_4

custom parts:
  4xAA Switchable Battery Pack w/JST connector: 4xAA Switchable Battery Pack with JST connector
  7-Segment LED I2C Backpack (yellow): 4-digit, 7-segment LED Display with I2C Control
  HUZZAH ESP8266 Breakout: The ESP8266 processor from Espressif is an 80 MHz microcontroller with a full WiFi front-end (both as client and access point) and TCP/IP stack with DNS support as well.
  Neopixel Strip -- White (60/m): Neopixel Strip, White, 60 pixels per meter.
