# Fritzing sketch Groovesizer [RED] - 2014-02-05 (saved by Fritzing 0.9.2b)
circuit board: 12cm x 8cm
breadboards: 1

parts:
  16MHZ_XTAL = Crystal [frequency="16 Mhz" package=THT]
  22 = Ceramic Capacitor [capacitance=22µF package="100 mil [THT, multilayer]"]
  22_2 = Ceramic Capacitor [capacitance=22µF package="100 mil [THT, multilayer]"]
  9V_DC = Power plug
  1N4001 = Rectifier Diode [part_number=1N4001 package="300 mil [THT]"]
  10uF = Electrolytic Capacitor [capacitance=10µF package="100 mil [THT, electrolytic]"]
  on/off = male pin header, 2 pins [form="♂ (male)"]
  104 = Ceramic Capacitor [capacitance=0.1µF package="100 mil [THT, multilayer]"]
  100uF = Electrolytic Capacitor [capacitance=10µF package="100 mil [THT, electrolytic]"]
  Pot1 = Alps Rotary Potentiometer [part_number=" RK09K1130AAU"]
  Pot2 = Alps Rotary Potentiometer [part_number=" RK09K1130AAU"]
  Pot3 = Alps Rotary Potentiometer [part_number=" RK09K1130AAU"]
  Pot4 = Alps Rotary Potentiometer [part_number=" RK09K1130AAU"]
  Pot5 = Alps Rotary Potentiometer [part_number=" RK09K1130AAU"]
  Switch1 = Pushbutton 12mm omron
  Switch2 = Pushbutton 12mm omron
  Switch3 = Pushbutton 12mm omron
  Switch4 = Pushbutton 12mm omron
  Switch5 = Pushbutton 12mm omron
  L1 = LED - 3mm [color="Red (633nm)" package="3 mm [THT]"]
  Audio = Audio Jack (TRS) 3.5mm [package="4Ucon 08780 [THT]"]
  74HC595_LED_1-8 = 74HC595 [package="DIP16 [THT]"]
  74HC595_LED_9-16 = 74HC595 [package="DIP16 [THT]"]
  Resist_2_-_220Ω = female pin header, 9 pins [form="♀ (female)"]
  Resist_1_-_220Ω = female pin header, 9 pins [form="♀ (female)"]
  L2 = LED - 3mm [color="Red (633nm)" package="3 mm [THT]"]
  L3 = LED - 3mm [color="Red (633nm)" package="3 mm [THT]"]
  L4 = LED - 3mm [color="Red (633nm)" package="3 mm [THT]"]
  L5 = LED - 3mm [color="Red (633nm)" package="3 mm [THT]"]
  L6 = LED - 3mm [color="Red (633nm)" package="3 mm [THT]"]
  L7 = LED - 3mm [color="Red (633nm)" package="3 mm [THT]"]
  L8 = LED - 3mm [color="Red (633nm)" package="3 mm [THT]"]
  L9 = LED - 3mm [color="Red (633nm)" package="3 mm [THT]"]
  L10 = LED - 3mm [color="Red (633nm)" package="3 mm [THT]"]
  L11 = LED - 3mm [color="Red (633nm)" package="3 mm [THT]"]
  L12 = LED - 3mm [color="Red (633nm)" package="3 mm [THT]"]
  L13 = LED - 3mm [color="Red (633nm)" package="3 mm [THT]"]
  L14 = LED - 3mm [color="Red (633nm)" package="3 mm [THT]"]
  L15 = LED - 3mm [color="Red (633nm)" package="3 mm [THT]"]
  L16 = LED - 3mm [color="Red (633nm)" package="3 mm [THT]"]
  104_2 = Ceramic Capacitor [capacitance=0.1µF package="100 mil [THT, multilayer]"]
  104_3 = Ceramic Capacitor [capacitance=0.1µF package="100 mil [THT, multilayer]"]
  1k2 = Resistor [tolerance=±5% resistance=1k package=THT]
  R1 = Resistor [tolerance=±5% resistance=220 package=THT]
  6N137 = IC, DIP package, 8 pins [chip_label=6N137]
  R2 = Resistor [tolerance=±5% resistance=10k package=THT]
  ICSP = double row female pin header, 6 pins [form="♀ (female)"]
  Expansion = female pin header, 6 pins [form="♀ (female)"]
  ATMEGA328P-PU = IC, DIP package, 28 pins [chip_label=IC]
  R3 = Resistor [tolerance=±5% resistance=220 package=THT]
  100uF_2 = Electrolytic Capacitor [capacitance=1µF package="100 mil [THT, electrolytic]"]
  104_4 = Ceramic Capacitor [capacitance=0.1µF package="100 mil [THT, multilayer]"]
  1N4148 = Rectifier Diode [part_number=1N4001 package="300 mil [THT]"]
  R4 = Resistor [tolerance=±5% resistance=220 package=THT]
  MIDI_OUT = DIN-5 jack (MIDI)
  MIDI_IN = DIN-5 jack (MIDI)
  7805 = Voltage Regulator [package=78xxl]

nets:
  N1: 16MHZ_XTAL.pin_0, 22_2.1, ATMEGA328P-PU.pin9
  N2: 16MHZ_XTAL.pin_1, 22.0, ATMEGA328P-PU.pin10
  GND: 22.1, 22_2.0, 9V_DC.GND, 10uF.-, 104.0, 100uF.-, Pot1.leg1, Pot2.leg1, Pot3.leg1, Pot4.leg1, Pot5.leg1, Switch1.Pin_1, Switch2.Pin_1, Switch3.Pin_1, Switch4.Pin_1, Switch5.Pin_1, Audio.Sleeve, 74HC595_LED_1-8.GND, 74HC595_LED_1-8.OE, 74HC595_LED_9-16.GND, 74HC595_LED_9-16.OE, Resist_2_-_220Ω.pin1, Resist_1_-_220Ω.pin1, 104_2.1, 104_3.1, 6N137.pin5, ICSP.pin4, Expansion.pin2, ATMEGA328P-PU.pin8, ATMEGA328P-PU.pin22, 104_4.1, MIDI_OUT.2, 7805.GND
  N3: 9V_DC.VCC, 1N4001.anode
  N4: 1N4001.cathode, on/off.pin1
  9V: 10uF.+, on/off.pin2, 7805.IN
  5V: 104.1, 100uF.+, Pot1.leg2, Pot2.leg2, Pot3.leg2, Pot4.leg2, Pot5.leg2, 74HC595_LED_1-8.MR, 74HC595_LED_1-8.VCC, 74HC595_LED_9-16.MR, 74HC595_LED_9-16.VCC, 104_2.0, 104_3.0, 1k2.Pin_1, R1.Pin_0, 6N137.pin8, R2.Pin_1, ICSP.pin6, Expansion.pin1, ATMEGA328P-PU.pin7, ATMEGA328P-PU.pin20, ATMEGA328P-PU.pin21, 7805.OUT
  Pot1: Pot1.wiper, ATMEGA328P-PU.pin23
  Pot2: Pot2.wiper, ATMEGA328P-PU.pin24
  Pot3: Pot3.wiper, ATMEGA328P-PU.pin25
  Pot4: Pot4.wiper, ATMEGA328P-PU.pin26
  Pot5: Pot5.wiper, ATMEGA328P-PU.pin27
  D6: Switch1.Pin_3, ATMEGA328P-PU.pin12
  D7: Switch2.Pin_3, ATMEGA328P-PU.pin13
  D8: Switch3.Pin_3, ATMEGA328P-PU.pin14
  D9: Switch4.Pin_3, ATMEGA328P-PU.pin15
  D10: Switch5.Pin_3, ATMEGA328P-PU.pin16
  N5: L1.cathode, Resist_1_-_220Ω.pin9
  N6: L1.anode, 74HC595_LED_1-8.Q0
  N7: Audio.Ring, Audio.Tip, 100uF_2.-
  N8: 74HC595_LED_1-8.Q1, L2.anode
  N9: 74HC595_LED_1-8.Q2, L3.anode
  N10: 74HC595_LED_1-8.Q3, L4.anode
  N11: 74HC595_LED_1-8.Q4, L5.anode
  N12: 74HC595_LED_1-8.Q5, L6.anode
  N13: 74HC595_LED_1-8.Q6, L7.anode
  N14: 74HC595_LED_1-8.Q7, L8.anode
  N15: 74HC595_LED_1-8.Q7', 74HC595_LED_9-16.DS
  D5: 74HC595_LED_1-8.SH_CP, 74HC595_LED_9-16.SH_CP, ATMEGA328P-PU.pin11
  D2: 74HC595_LED_1-8.ST_CP, 74HC595_LED_9-16.ST_CP, ATMEGA328P-PU.pin4
  D4: 74HC595_LED_1-8.DS, ATMEGA328P-PU.pin6
  N16: 74HC595_LED_9-16.Q1, L10.anode
  N17: 74HC595_LED_9-16.Q2, L11.anode
  N18: 74HC595_LED_9-16.Q3, L12.anode
  N19: 74HC595_LED_9-16.Q4, L13.anode
  N20: 74HC595_LED_9-16.Q5, L14.anode
  N21: 74HC595_LED_9-16.Q6, L15.anode
  N22: 74HC595_LED_9-16.Q7, L16.anode
  N23: 74HC595_LED_9-16.Q0, L9.anode
  N24: Resist_2_-_220Ω.pin2, L16.cathode
  N25: Resist_2_-_220Ω.pin3, L15.cathode
  N26: Resist_2_-_220Ω.pin4, L14.cathode
  N27: Resist_2_-_220Ω.pin5, L13.cathode
  N28: Resist_2_-_220Ω.pin6, L12.cathode
  N29: Resist_2_-_220Ω.pin7, L11.cathode
  N30: Resist_2_-_220Ω.pin8, L10.cathode
  N31: Resist_2_-_220Ω.pin9, L9.cathode
  N32: Resist_1_-_220Ω.pin2, L8.cathode
  N33: Resist_1_-_220Ω.pin3, L7.cathode
  N34: Resist_1_-_220Ω.pin4, L6.cathode
  N35: Resist_1_-_220Ω.pin5, L5.cathode
  N36: Resist_1_-_220Ω.pin6, L4.cathode
  N37: Resist_1_-_220Ω.pin7, L3.cathode
  N38: Resist_1_-_220Ω.pin8, L2.cathode
  N39: 1k2.Pin_0, ICSP.pin3, ATMEGA328P-PU.pin1
  N40: R1.Pin_1, MIDI_OUT.5
  N41: 6N137.pin2, 1N4148.cathode, R4.Pin_1
  N42: 6N137.pin3, 1N4148.anode, MIDI_IN.4
  D0 (RX): 6N137.pin6, R2.Pin_0, ATMEGA328P-PU.pin2
  D12: ICSP.pin1, Expansion.pin4, ATMEGA328P-PU.pin18
  D13: ICSP.pin2, Expansion.pin5, ATMEGA328P-PU.pin19
  D11: ICSP.pin5, Expansion.pin3, ATMEGA328P-PU.pin17
  A5: Expansion.pin6, ATMEGA328P-PU.pin28
  D1 (TX): ATMEGA328P-PU.pin3, MIDI_OUT.4
  D3: ATMEGA328P-PU.pin5, R3.Pin_1
  N43: R3.Pin_0, 100uF_2.+, 104_4.0
  N44: R4.Pin_0, MIDI_IN.5

notes:
  ATMEGA328P-PU
  POWER SUPPLY
  5V
  GND
  D11
  D12
  D13
  A5
  [RED]
  MIDI IN
  MIDI OUT
  _________
  ___________
  groovesizer [RED] - groovesizer.com

custom parts:
  Alps Rotary Potentiometer: A rotary adjustable resistor (potentiometer).
  Pushbutton 12mm omron: A generic pushbutton. 12mm
  DIN-5 jack (MIDI): Female DIN connector with 5 pins, as used for MIDI and SYNC
