# Fritzing sketch Groovesizer [TB2] - RV1 (saved by Fritzing 0.9.0b)
circuit board: 13cm x 9.9cm
breadboards: 1

parts:
  DUE = Arduino Due (Rev2b)
  S1 = Pushbutton [package="[THT]"]
  S2 = Pushbutton [package="[THT]"]
  S3 = Pushbutton [package="[THT]"]
  S4 = Pushbutton [package="[THT]"]
  S5 = Pushbutton [package="[THT]"]
  S6 = Pushbutton [package="[THT]"]
  S7 = Pushbutton [package="[THT]"]
  S8 = Pushbutton [package="[THT]"]
  S9 = Pushbutton [package="[THT]"]
  S10 = Pushbutton [package="[THT]"]
  S11 = Pushbutton [package="[THT]"]
  S12 = Pushbutton [package="[THT]"]
  S13 = Pushbutton [package="[THT]"]
  Pot2 = Alps Rotary Potentiometer [part_number=" RK09K1130AAU"]
  Pot3 = Alps Rotary Potentiometer [part_number=" RK09K1130AAU"]
  Pot4 = Alps Rotary Potentiometer [part_number=" RK09K1130AAU"]
  Pot1 = Alps Rotary Potentiometer [part_number=" RK09K1130AAU"]
  Pot5 = Alps Rotary Potentiometer [part_number=" RK09K1130AAU"]
  1N4149 = Rectifier Diode [part_number=1N4001 package="300 mil [THT]"]
  R11 = Resistor [tolerance=±5% resistance=220 package=THT]
  R14 = Resistor [tolerance=±5% resistance=51 package=THT]
  R15 = Resistor [tolerance=±5% resistance=51 package=THT]
  R16 = Resistor [tolerance=±5% resistance=220 package=THT]
  6N139 = IC, DIP package, 8 pins [chip_label=6N138]
  500Ω = Resistor [tolerance=±5% resistance=470 package=THT]
  500Ω_2 = Resistor [tolerance=±5% resistance=470 package=THT]
  CONTRAST = female pin header, 3 pins [form="♀ (female)"]
  SPI = double row female pin header, 6 pins [form="♀ (female)"]
  LED = LED - 3mm [color="Red (633nm)" package="3 mm [THT]"]
  R17 = Resistor [tolerance=±5% resistance=220 package=THT]
  S14 = Pushbutton [package="[THT]"]
  MIDI_IN = DIN-5 jack (MIDI)
  MIDI_OUT = DIN-5 jack (MIDI)
  SD = SD_CARD_SOCKET [package=sdcard_4uconn]
  Pad1 = Pad [width=2.87710705840859 height=3.53860323443398 connect=center]  # not connected
  Pad2 = Pad [width=2.87710705840859 height=3.53860323443398 connect=center]  # not connected
  S15 = Pushbutton [package="[THT]"]
  C1 = Electrolytic Capacitor [capacitance=47µF voltage=16V package="100 mil [THT, electrolytic]"]
  104 = Ceramic Capacitor [capacitance=100nF package="100 mil [THT, multilayer]"]
  LCD = LCD screen
  GND_/_SLEEVE = female pin header, 1 pin [form="♀ (female)"]
  TIP = female pin header, 1 pin [form="♀ (female)"]
  RING = female pin header, 1 pin [form="♀ (female)"]
  EXPANSION = double row female pin header, 34 pins [form="♀ (female)"]
  J1 = double row female pin header, 4 pins [form="♀ (female)"]
  J2 = female pin header, 2 pins [form="♀ (female)"]

nets:
  N1: DUE.A8, EXPANSION.pin20
  N2: DUE.A9, EXPANSION.pin14
  N3: DUE.A10, EXPANSION.pin21
  N4: DUE.A11, EXPANSION.pin13
  DAC0: DUE.DAC0, 500Ω.Pin_0
  DAC1: DUE.DAC1, 500Ω_2.Pin_0
  A0: DUE.A0, Pot1.wiper
  A1: DUE.A1, Pot2.wiper
  A2: DUE.A2, Pot3.wiper
  A3: DUE.A3, Pot4.wiper
  A4: DUE.A4, Pot5.wiper
  N5: DUE.A5, EXPANSION.pin16
  N6: DUE.A6, EXPANSION.pin19
  N7: DUE.A7, EXPANSION.pin15
  N8: DUE.D14/TX3, J1.pin2
  N9: DUE.D15/RX3, J1.pin3
  TX2: DUE.D16/TX2, EXPANSION.pin4
  N10: DUE.D17/RX2, EXPANSION.pin31
  TX1: DUE.D18/TX1, R14.Pin_0
  RX1: DUE.D19/RX1, R16.Pin_0, 6N139.pin6
  3.3V: DUE.IOREF, Pot2.leg2, Pot3.leg2, Pot4.leg2, Pot1.leg2, Pot5.leg2, R15.Pin_0, R16.Pin_1, 6N139.pin8, SD.VDD, C1.+, 104.1, EXPANSION.pin17
  5V: DUE.5V, CONTRAST.pin3, LCD.VDD, LCD.LED+, J2.pin1
  GND: DUE.GND, S1.Pin_1, S1.Pin_2, S2.Pin_1, S2.Pin_2, S3.Pin_1, S3.Pin_2, S4.Pin_1, S4.Pin_2, S5.Pin_1, S5.Pin_2, S6.Pin_1, S6.Pin_2, S7.Pin_1, S7.Pin_2, S8.Pin_1, S8.Pin_2, S9.Pin_1, S9.Pin_2, S10.Pin_1, S10.Pin_2, S11.Pin_1, S11.Pin_2, S12.Pin_1, S12.Pin_2, S13.Pin_1, S13.Pin_2, Pot2.leg1, Pot3.leg1, Pot4.leg1, Pot1.leg1, Pot5.leg1, 6N139.pin5, CONTRAST.pin1, LED.cathode, S14.Pin_1, S14.Pin_2, MIDI_OUT.2, SD.VSS1, SD.VSS2, S15.Pin_1, S15.Pin_2, C1.-, 104.0, LCD.VSS, LCD.R/W, LCD.LED-, GND_/_SLEEVE.pin1, EXPANSION.pin18, J2.pin2
  N11: DUE.D8_PWM, EXPANSION.pin2
  N12: DUE.D9_PWM, EXPANSION.pin33
  SD CS: DUE.D10_PWM/SS0, SD.CD_DAT3
  LCD E: DUE.D11_PWM, LCD.E
  LCD RS: DUE.D12_PWM, LCD.RS
  LED: DUE.D13_PWM, R17.Pin_1
  N13: DUE.D0/RX, J1.pin4
  N14: DUE.D1/TX, J1.pin1
  LCD D7: DUE.D2_PWM, LCD.DB7
  LCD D6: DUE.D3_PWM, LCD.DB6
  LCD D5: DUE.D4_PWM/SS1, LCD.DB5
  LCD D4: DUE.D5_PWM, LCD.DB4
  N15: DUE.D6_PWM, EXPANSION.pin1
  N16: DUE.D7_PWM, EXPANSION.pin34
  D22: DUE.D22, S1.Pin_3, S1.Pin_4
  D23: DUE.D23, S9.Pin_3, S9.Pin_4
  D24: DUE.D24, S2.Pin_3, S2.Pin_4
  D25: DUE.D25, S10.Pin_3, S10.Pin_4
  D26: DUE.D26, S3.Pin_3, S3.Pin_4
  D27: DUE.D27, S4.Pin_3, S4.Pin_4
  D28: DUE.D28, S11.Pin_3, S11.Pin_4
  D29: DUE.D29, S5.Pin_3, S5.Pin_4
  D30: DUE.D30, S12.Pin_3, S12.Pin_4
  D31: DUE.D31, S6.Pin_3, S6.Pin_4
  D32: DUE.D32, S13.Pin_3, S13.Pin_4
  D33: DUE.D33, S7.Pin_3, S7.Pin_4
  D34: DUE.D34, S8.Pin_3, S8.Pin_4
  D35: DUE.D35, S14.Pin_3, S14.Pin_4
  D36: DUE.D36, S15.Pin_3, S15.Pin_4
  N17: DUE.D37, EXPANSION.pin30
  N18: DUE.D38, EXPANSION.pin5
  N19: DUE.D39, EXPANSION.pin29
  N20: DUE.D40, EXPANSION.pin6
  N21: DUE.D41, EXPANSION.pin28
  N22: DUE.D42, EXPANSION.pin7
  N23: DUE.D43, EXPANSION.pin27
  N24: DUE.D44, EXPANSION.pin8
  N25: DUE.D45, EXPANSION.pin26
  N26: DUE.D46, EXPANSION.pin9
  N27: DUE.D47, EXPANSION.pin25
  N28: DUE.D48, EXPANSION.pin10
  N29: DUE.D49, EXPANSION.pin24
  N30: DUE.D50, EXPANSION.pin11
  N31: DUE.D51, EXPANSION.pin23
  N32: DUE.D52, EXPANSION.pin12
  N33: DUE.D53, EXPANSION.pin22
  N34: 1N4149.cathode, R11.Pin_1, 6N139.pin2
  N35: 1N4149.anode, 6N139.pin3, MIDI_IN.4
  N36: R11.Pin_0, MIDI_IN.5
  N37: R14.Pin_1, MIDI_OUT.4
  N38: R15.Pin_1, MIDI_OUT.5
  N39: 500Ω.Pin_1, TIP.pin1
  N40: 500Ω_2.Pin_1, RING.pin1
  N41: CONTRAST.pin2, LCD.V0
  N42: SPI.pin2, SD.CMD
  N43: SPI.pin5, SD.CLK
  N44: SPI.pin6, SD.DAT0
  N45: LED.anode, R17.Pin_0

notes:
  -----------
  ---------
  MIDI IN
  MIDI OUT
  --------------
  ----------------
  (insert upside down)
  3V3
  GND
  A5
  A6
  A7
  A8
  A9
  A10
  A11
  53
  52
  51
  47
  45
  43
  41
  39
  37
  50
  48
  46
  44
  42
  40
  38
  AUDIO OUT
  SD
  RX2
  TX2
  6
  7
  8
  9
  TX0
  RX0
  TX3
  RX3
  N/C
  5V
  49
  groovesizer.com TB2 ver.1

custom parts:
  Alps Rotary Potentiometer: A rotary adjustable resistor (potentiometer).
  DIN-5 jack (MIDI): Female DIN connector with 5 pins, as used for MIDI and SYNC
