# Fritzing sketch RaspberryPi (saved by Fritzing 0.9.2b)
breadboards: 2

parts:
  VCC1 = Battery
  Power_plug1 = Power plug
  Raspberry_Pi1 = Raspberry Pi B+  # not connected
  Pi1 = Adafruit Pi Cobbler  # not connected
  IC3 = MCP3008 8-channel 10-bit ADC [part_number=MCP3008]  # not connected
  RaspberryPi1 = Raspberry Pi Model B  # not connected
  DAC1 = MCP4725 12-bit DAC Breakout  # not connected
  BATT1 = 4xAA Switchable Battery Pack w/JST connector  # not connected
  Bauteil2 = 16-Channel 12-bit PCA9685 PWM/Servo Driver  # not connected
  Bauteil4 = PiTFT 2.2in HAT  # not connected
  IC4 = Voltage Regulator [package=to-220-alt]  # not connected
  D1 = Rectifier Diode [part_number=1N4001 package="300 mil [THT]"]
  R10 = Resistor [tolerance=±5% resistance=470 package=THT]
  C1 = Electrolytic Capacitor [capacitance=1mF package="100 mil [THT, electrolytic]"]
  R15 = Rotary Potentiometer (Small) [maximum_resistance=100kΩ package=THT]
  S16 = Pushbutton [package="[THT]"]
  Bauteil5 = Logic Level Converter  # not connected
  LPD8806_RGB_LED_Strip1 = LPD8806 RGB LED Strip  # not connected
  U13 = HALL-EFFECT [package=sc70]
  NEOPIXEL1 = Neopixel Strip -- White (60/m)
  BB1 = 4-Line Bi-Directional Level Shifter  # not connected
  JACK2 = 2.1mm Barrel Jack with Terminal Block  # not connected
  IC5 = Voltage Regulator [package=to-220-alt]  # not connected
  S17 = Pushbutton [package="[THT]"]
  S18 = Pushbutton [package="[THT]"]
  S19 = Pushbutton [package="[THT]"]
  S20 = Pushbutton [package="[THT]"]
  S21 = Pushbutton [package="[THT]"]
  S22 = Pushbutton [package="[THT]"]

nets:
  GND: VCC1.-, R15.leg2, S16.Pin_1, S16.Pin_2, U13.GND, NEOPIXEL1.GND
  N1: VCC1.+, C1.-
  N2: Power_plug1.VCC, D1.anode
  N3: R10.Pin_1, NEOPIXEL1.DI
  VCC: C1.+, R15.leg1, U13.VCC, NEOPIXEL1.+5V
  N4: S16.Pin_3, S16.Pin_4, U13.OUT
  N5: S17.Pin_1, S17.Pin_2
  N6: S17.Pin_3, S17.Pin_4
  N7: S18.Pin_1, S18.Pin_2
  N8: S18.Pin_3, S18.Pin_4
  N9: S19.Pin_1, S19.Pin_2
  N10: S19.Pin_3, S19.Pin_4
  N11: S20.Pin_1, S20.Pin_2
  N12: S20.Pin_3, S20.Pin_4
  N13: S21.Pin_1, S21.Pin_2
  N14: S21.Pin_3, S21.Pin_4
  N15: S22.Pin_1, S22.Pin_2
  N16: S22.Pin_3, S22.Pin_4

notes:
  Soundblaster Play
  WLAN
  BT
  USB-Hub
  Neopixel Strip 144/m
  (0.5m = 72px:
  32px, 40px)
  References:
  Neopixel Painter
  https://learn.adafruit.com/neopixel-painter
  Raspberry Pi
  Neopixel library
  Wiimote
  Python
  Pygame
  cwiid
  Pure Data
  libpd
  voltage regulators:
  LM1117 (3.3V out)
  L7805 (5V out)
  UBEC
  voltage divider:
  Vin - R1 - R2 -Vout
  5V - R2k - R1k - 3.3V
  5V -R470 - R330 - 3.3V
  https://learn.sparkfun.com/tutorials/voltage-dividers
  Level Shifters:
  74AHCT125 (quad 3 to 5V)
  Power supply:
  MB102 (3.3V or 5V)
  voltage regulators
  UBEC (5V @ 3A)
  - - - - - - - - -
  Battery Pack:
  4 x Eneloop (4.8V)
  4 x Duracell (6V)
  USB-Power-Bank (5V @ 1A, 2A, bis 10.000Ah)
  RC-Akku + UBEC
  DotStar
  APA102
  (1m a 144px)
  References:
  DotStar Pi Painter
  LPD8806
  References/ Projects:
  LightPainting with Raspberry Pi
  Boblight
  DAC
  4725
  ADC
  MCP3008
  ? bit
  ? channels
  Resistors:
  10k pullups
  LED-Vrowiderstand 220 - 1000 Ohm
  Capacitors:
  10uF über Power Supply
  1000uF bei Neopixels
  74AHCT125 (quad level shifter 3 to 5V)

custom parts:
  Adafruit Pi Cobbler: Adafruit Pi Cobbler GPIO Breakout for Raspberry Pi
  Raspberry Pi Model B: Raspberry Pi (Model B)
  MCP4725 12-bit DAC Breakout: MCP4725 12-bit Digital-to-Analog Converter
  4xAA Switchable Battery Pack w/JST connector: 4xAA Switchable Battery Pack with JST connector
  16-Channel 12-bit PCA9685 PWM/Servo Driver: The Adafruit 16-Channel 12-bit PWM/Servo Driver will drive up to 16 servos over I2C with only 2 pins. The on-board PCA9685 PWM controller will drive all 16 channels simultaneously with no additional processing overhead. What's more, you can chain up to 62 of them to control up to 992 servos - all with the same 2 pins
  PiTFT 2.2in HAT: Primary display for Raspberry Pi in HAT form featuring a 2.2" display with 320x240 16-bit color pixels. The HAT uses the high speed SPI interface on the Pi and can use the mini display as a console, X window port, displaying images or video etc. Best of all it plugs right in on top of your Model A+ or B+ and fits into our case quite nicely.
  LPD8806 RGB LED Strip: Digitally addressable RGB LED strip
  Neopixel Strip -- White (60/m): Neopixel Strip, White, 60 pixels per meter.
  4-Line Bi-Directional Level Shifter: 4-Channel Bi-Directional Level Shifter
