# Fritzing sketch Synth-DIY_Workstation_Schaltplan (saved by Fritzing 0.9.2b)
breadboards: 3

parts:
  Bauteil1 = Arduino Nano (Rev3.0)  # not connected
  U1 = MIDI_CONN_FEMALE_SUPPORT [package=din_5_female_support]  # not connected
  U3 = Alphanumeric LED Display [package=alphanumeric]  # not connected
  IC1 = SELECTOR_MULTIPLEXER [package=lcc20]  # not connected
  U4 = 74HC595 [package="DIP16 [THT]"]  # not connected
  U5 = 74HC595 [package="DIP16 [THT]"]  # not connected
  U6 = Alphanumeric LED Display [package=alphanumeric]  # not connected
  U7 = Alphanumeric LED Display [package=alphanumeric]  # not connected
  U8 = Alphanumeric LED Display [package=alphanumeric]  # not connected
  U9 = 74HC595 [package="DIP16 [THT]"]  # not connected
  IC2 = SELECTOR_MULTIPLEXER [package=lcc20]  # not connected
  U10 = MIDI_CONN_FEMALE_SUPPORT [package=din_5_female_support]  # not connected
  R1 = Rotary Potentiometer (Small) [maximum_resistance=100kΩ package=THT]  # not connected
  VCC1 = Battery  # not connected
  Power_plug1 = Power plug
  Raspberry_Pi1 = Raspberry Pi B+  # not connected
  TRS1 = Audio Jack (TRS) 3.5mm [package="4Ucon 08780 [THT]"]  # not connected
  SW1 = ENCODER_RGB_CA [package=encoder_led_3]  # not connected
  SP1 = SPEAKER [package=pcb_mount_speaker]  # not connected
  S1 = Round Pushbutton  # not connected
  R3 = Rotary Potentiometer (Small) [maximum_resistance=100kΩ package=THT]  # not connected
  S2 = Round Pushbutton  # not connected
  R4 = Rotary Potentiometer (Small) [maximum_resistance=100kΩ package=THT]  # not connected
  S3 = Round Pushbutton  # not connected
  R5 = Rotary Potentiometer (Small) [maximum_resistance=100kΩ package=THT]  # not connected
  S4 = Round Pushbutton  # not connected
  R6 = Rotary Potentiometer (Small) [maximum_resistance=100kΩ package=THT]  # not connected
  S5 = Round Pushbutton  # not connected
  R7 = Rotary Potentiometer (Small) [maximum_resistance=100kΩ package=THT]  # not connected
  S6 = Round Pushbutton  # not connected
  R8 = Rotary Potentiometer (Small) [maximum_resistance=100kΩ package=THT]  # not connected
  S7 = Round Pushbutton  # not connected
  R9 = Rotary Potentiometer (Small) [maximum_resistance=100kΩ package=THT]  # not connected
  S8 = Round Pushbutton  # not connected
  S9 = Round Pushbutton  # not connected
  S10 = Round Pushbutton  # not connected
  S11 = Round Pushbutton  # not connected
  S12 = Round Pushbutton  # not connected
  S13 = Round Pushbutton  # not connected
  J1 = shrouded pin header, 10 pins [form="♂ (shrouded male)"]  # not connected
  S14 = Round Pushbutton  # not connected
  S15 = Round Pushbutton  # not connected
  VCC2 = Battery  # not connected
  Pi1 = Adafruit Pi Cobbler  # not connected
  IC3 = MCP3008 8-channel 10-bit ADC [part_number=MCP3008]  # not connected
  RaspberryPi1 = Raspberry Pi Model B  # not connected
  DAC1 = MCP4725 12-bit DAC Breakout  # not connected
  BATT1 = 4xAA Switchable Battery Pack w/JST connector  # not connected
  BUTTON1 = Waterproof Pushbutton (green)  # not connected
  BLUEFRUIT1 = Adafruit Bluefruit EZ-LINK v1.0  # not connected
  POT1 = Analog Thumb Joystick  # not connected
  Bauteil2 = 16-Channel 12-bit PCA9685 PWM/Servo Driver  # not connected
  Bauteil4 = PiTFT 2.2in HAT  # not connected
  IC4 = Voltage Regulator [package=to-220-alt]  # not connected
  LED1 = RGB LED (com. cathode, rgb) [package="5 mm [THT]"]  # not connected
  D1 = Rectifier Diode [part_number=1N4001 package="300 mil [THT]"]
  R10 = Resistor [tolerance=±5% resistance=220 package=THT]  # not connected
  C1 = Electrolytic Capacitor [capacitance=1µF package="100 mil [THT, electrolytic]"]  # not connected
  R11 = Rotary Potentiometer (Small) [maximum_resistance=100kΩ package=THT]  # not connected
  R12 = Rotary Potentiometer (Small) [maximum_resistance=100kΩ package=THT]  # not connected
  R13 = Rotary Potentiometer (Small) [maximum_resistance=100kΩ package=THT]  # not connected
  R14 = Rotary Potentiometer (Small) [maximum_resistance=100kΩ package=THT]  # not connected
  R15 = Rotary Potentiometer (Small) [maximum_resistance=100kΩ package=THT]  # not connected
  S16 = Pushbutton [package="[THT]"]
  Bauteil5 = Logic Level Converter  # not connected
  LPD8806_RGB_LED_Strip1 = LPD8806 RGB LED Strip  # not connected
  U13 = HALL-EFFECT [package=sc70]  # not connected
  NEOPIXEL1 = Neopixel Strip -- White (60/m)  # not connected
  JACK1 = 2.1mm Barrel Jack with Terminal Block  # not connected
  Bauteil6 = blueIOT core  # not connected
  Bauteil7 = Memoire 1.0 - SD card log shield  # not connected
  Bauteil8 = Arduino Uno (Rev3) - ICSP  # not connected
  Bauteil9 = HUZZAH ESP8266 Breakout  # not connected
  TRELLIS1 = Adafruit Trellis  # not connected

nets:
  N1: Power_plug1.VCC, D1.cathode
  N2: S16.Pin_1, S16.Pin_2
  N3: S16.Pin_3, S16.Pin_4

notes:
  MFOS 3-Ch. Amplifier
  MFOS Noise Toaster
  Soundblaster Play
  WLAN
  BT
  USB-Hub
  Neopixel Strip 144/m
  (32 pixel)
  UBEC
  CV/ Gate Mod.
  Wiimote
  TouchOSC
  Python
  Pygame
  cwiid
  Pure Data
  libpd
  Netzteil(e):
  USB-Hub --> Arduino, Raspberry (700 mAh !)
  9V MFOS
  5V Neopixels (32*3*30 mAh = 3 Ah)
  Mini Beamer
  Laser

custom parts:
  Adafruit Pi Cobbler: Adafruit Pi Cobbler GPIO Breakout for Raspberry Pi
  Raspberry Pi Model B: Raspberry Pi (Model B)
  MCP4725 12-bit DAC Breakout: MCP4725 12-bit Digital-to-Analog Converter
  4xAA Switchable Battery Pack w/JST connector: 4xAA Switchable Battery Pack with JST connector
  Waterproof Pushbutton (green): Waterproof Illuminated Pushbutton (green)
  Adafruit Bluefruit EZ-LINK v1.0: Bluefruit EZ-LINK, Bluetooth Serial Link & Arduino Programmer
  16-Channel 12-bit PCA9685 PWM/Servo Driver: The Adafruit 16-Channel 12-bit PWM/Servo Driver will drive up to 16 servos over I2C with only 2 pins. The on-board PCA9685 PWM controller will drive all 16 channels simultaneously with no additional processing overhead. What's more, you can chain up to 62 of them to control up to 992 servos - all with the same 2 pins
  PiTFT 2.2in HAT: Primary display for Raspberry Pi in HAT form featuring a 2.2" display with 320x240 16-bit color pixels. The HAT uses the high speed SPI interface on the Pi and can use the mini display as a console, X window port, displaying images or video etc. Best of all it plugs right in on top of your Model A+ or B+ and fits into our case quite nicely.
  LPD8806 RGB LED Strip: Digitally addressable RGB LED strip
  Neopixel Strip -- White (60/m): Neopixel Strip, White, 60 pixels per meter.
  HUZZAH ESP8266 Breakout: The ESP8266 processor from Espressif is an 80 MHz microcontroller with a full WiFi front-end (both as client and access point) and TCP/IP stack with DNS support as well.
